# Fritzing sketch PCB_Design (saved by Fritzing 0.9.2b)
circuit board: 5.36311cm x 6.88566cm
breadboards: 1

parts:
  100nF = Ceramic Capacitor [capacitance=100nF package="100 mil [THT, multilayer]"]
  10uF = Electrolytic Capacitor [capacitance=10µF package="100 mil [THT, electrolytic]"]
  KWM-20882CBA = female pin header, 8 pins [form="♀ (female)"]
  k1_K2_K3_K4_K5__K6_K7_K8_K9_K10_K11_K12_K13_K14 = female pin header, 8 pins [form="♀ (female)"]
  Q5 = MOSFET-NCHANNEL [package=to220v]
  #2 = MOSFET-NCHANNEL [package=to220v]
  #3 = MOSFET-NCHANNEL [package=to220v]
  #4 = MOSFET-NCHANNEL [package=to220v]
  Relay = RELAY [package=relay-g5q]
  C_B_E = TRANSISTOR_NPN [package=to-92-ammo]
  J1_J2_J3__J4_J5_J6_J7__J8_J9_J10_J11 = female pin header, 11 pins [form="♀ (female)"]
  G_D_+V = female pin header, 3 pins [form="♀ (female)"]
  R2 = female pin header, 14 pins [form="♀ (female)"]
  R1 = female pin header, 2 pins [form="♀ (female)"]
  KWM-20882CBA_2 = Arduino Uno (Rev3)
  R3 = female pin header, 1 pin [form="♀ (female)"]
  #1 = female pin header, 2 pins [form="♀ (female)"]
  MAX7219CNG = MAX 7219 [package="DIP (Dual Inline) [THT]"]

nets:
  N1: 100nF.0, 10uF.+, Relay.COIL2, G_D_+V.pin1, R1.pin1, KWM-20882CBA_2.5V, #1.pin2, MAX7219CNG.V+
  GND: 100nF.1, 10uF.-, Q5.S, #2.S, #3.S, #4.S, C_B_E.E, J1_J2_J3__J4_J5_J6_J7__J8_J9_J10_J11.pin4, J1_J2_J3__J4_J5_J6_J7__J8_J9_J10_J11.pin6, J1_J2_J3__J4_J5_J6_J7__J8_J9_J10_J11.pin8, J1_J2_J3__J4_J5_J6_J7__J8_J9_J10_J11.pin10, G_D_+V.pin3, R2.pin1, R2.pin4, R2.pin7, R2.pin10, KWM-20882CBA_2.GND, MAX7219CNG.GND
  N2: KWM-20882CBA.pin1, MAX7219CNG.SEG_C
  N3: KWM-20882CBA.pin2, MAX7219CNG.SEG_B
  N4: KWM-20882CBA.pin3, MAX7219CNG.SEG_A
  N5: KWM-20882CBA.pin4, MAX7219CNG.SEG_DP
  N6: KWM-20882CBA.pin5, MAX7219CNG.DIG_3
  N7: KWM-20882CBA.pin6, MAX7219CNG.DIG_2
  N8: KWM-20882CBA.pin7, MAX7219CNG.DIG_1
  N9: KWM-20882CBA.pin8, MAX7219CNG.DIG_0
  N10: k1_K2_K3_K4_K5__K6_K7_K8_K9_K10_K11_K12_K13_K14.pin1, MAX7219CNG.DIG_7
  N11: k1_K2_K3_K4_K5__K6_K7_K8_K9_K10_K11_K12_K13_K14.pin2, MAX7219CNG.DIG_6
  N12: k1_K2_K3_K4_K5__K6_K7_K8_K9_K10_K11_K12_K13_K14.pin3, MAX7219CNG.DIG_5
  N13: k1_K2_K3_K4_K5__K6_K7_K8_K9_K10_K11_K12_K13_K14.pin4, MAX7219CNG.DIG_4
  N14: k1_K2_K3_K4_K5__K6_K7_K8_K9_K10_K11_K12_K13_K14.pin5, MAX7219CNG.SEG_G
  N15: k1_K2_K3_K4_K5__K6_K7_K8_K9_K10_K11_K12_K13_K14.pin6, MAX7219CNG.SEG_F
  N16: k1_K2_K3_K4_K5__K6_K7_K8_K9_K10_K11_K12_K13_K14.pin7, MAX7219CNG.SEG_E
  N17: k1_K2_K3_K4_K5__K6_K7_K8_K9_K10_K11_K12_K13_K14.pin8, MAX7219CNG.SEG_D
  N18: Q5.G, R2.pin2, R2.pin3
  N19: Q5.D, J1_J2_J3__J4_J5_J6_J7__J8_J9_J10_J11.pin11
  N20: #2.G, R2.pin5, R2.pin6
  N21: #2.D, J1_J2_J3__J4_J5_J6_J7__J8_J9_J10_J11.pin9
  N22: #3.G, R2.pin8, R2.pin9
  N23: #3.D, J1_J2_J3__J4_J5_J6_J7__J8_J9_J10_J11.pin7
  N24: #4.G, R2.pin11, R2.pin12
  N25: #4.D, J1_J2_J3__J4_J5_J6_J7__J8_J9_J10_J11.pin5
  N26: Relay.MAIN, J1_J2_J3__J4_J5_J6_J7__J8_J9_J10_J11.pin3
  N27: Relay.NO, J1_J2_J3__J4_J5_J6_J7__J8_J9_J10_J11.pin2
  N28: Relay.NC, J1_J2_J3__J4_J5_J6_J7__J8_J9_J10_J11.pin1
  N29: Relay.COIL1, R2.pin13
  N30: C_B_E.B, R3.pin1
  N31: C_B_E.C, R2.pin14
  N32: G_D_+V.pin2, KWM-20882CBA_2.D8, #1.pin1
  N33: R1.pin2, MAX7219CNG.ISET
  N34: KWM-20882CBA_2.D12/MISO, MAX7219CNG.LOAD_(CS)
  N35: KWM-20882CBA_2.D13/SCK, MAX7219CNG.CLK
  N36: KWM-20882CBA_2.D2, MAX7219CNG.DIN

notes:
  C

custom parts:
  MAX 7219: A led matrix driver on a 300 mil dual inline package (DIP) footprint.
